# Fritzing sketch Etude_2 (saved by Fritzing 0.9.3b)
breadboards: 1

parts:
  LED1 = LED - 5mm [color="Red (633nm)" package="5 mm [THT]"]
  LED2 = LED - 5mm [color="Red (633nm)" package="5 mm [THT]"]
  LED3 = LED - 5mm [color="Red (633nm)" package="5 mm [THT]"]
  LED4 = LED - 5mm [color="Red (633nm)" package="5 mm [THT]"]
  LED5 = LED - 5mm [color="Red (633nm)" package="5 mm [THT]"]
  S1 = Pushbutton [package="[THT]"]  # not connected
  BAT1 = Battery Holders [package=battcon_245mm_pth]
  U1 = attiny85 [package=dip]
  R1 = Resistor [tolerance=±5% resistance=220 package=THT]

nets:
  N1: LED1.anode, LED4.cathode, LED5.cathode, U1.Pin_6
  N2: LED2.cathode, R1.Pin_1
  N3: LED2.anode, U1.Pin_7
  N4: LED3.anode, U1.Pin_3
  N5: LED4.anode, U1.Pin_2
  N6: LED5.anode, U1.Pin_1
  N7: BAT1.+, U1.Pin_8, R1.Pin_0

notes:
  I'm not sure how to draw the alternate system by reading the schematic
