# Fritzing sketch Etude_2_002 (saved by Fritzing 0.9.3b)
breadboards: 1

parts:
  BAT1 = Battery Holders [package=battcon_245mm_pth]
  R1 = Resistor [tolerance=±5% resistance=300 package=THT]
  R2 = Resistor [tolerance=±5% resistance=300 package=THT]
  R3 = Resistor [tolerance=±5% resistance=300 package=THT]
  R4 = Resistor [tolerance=±5% resistance=300 package=THT]
  R5 = Resistor [tolerance=±5% resistance=300 package=THT]
  LED1 = smd LED [color="Red (633nm)" package="0603 [SMD]"]
  LED2 = smd LED [color="Red (633nm)" package="0603 [SMD]"]
  LED3 = smd LED [color="Red (633nm)" package="0603 [SMD]"]
  LED4 = smd LED [color="Red (633nm)" package="0603 [SMD]"]
  LED5 = smd LED [color="Red (633nm)" package="0603 [SMD]"]
  U1 = attiny85 [package=dip]
  S1 = Pushbutton [package="[THT]"]

nets:
  N1: BAT1.+, S1.Pin_1, S1.Pin_2
  N2: BAT1.-, R1.Pin_0, R2.Pin_0, R3.Pin_0, R4.Pin_0, R5.Pin_0, U1.Pin_4
  N3: R1.Pin_1, LED1.cathode
  N4: R2.Pin_1, LED2.cathode
  N5: R3.Pin_1, LED3.cathode
  N6: R4.Pin_1, LED4.cathode
  N7: R5.Pin_1, LED5.cathode
  N8: LED1.anode, U1.Pin_3
  N9: LED2.anode, U1.Pin_2
  N10: LED3.anode, U1.Pin_7
  N11: LED4.anode, U1.Pin_6
  N12: LED5.anode, U1.Pin_5
  N13: U1.Pin_8, S1.Pin_3, S1.Pin_4
